// Logisim project processor_riscv_evolution.circ as structural Verilog: 6 circuits, main circuit main
module main (
  input  [31:0] in_1,
  input  [31:0] in_2,
  input  [31:0] in_3,
  output [31:0] out_4
);

  wire [2:0] controlunit_1_alucontrol;

  ControlUnit controlunit_1 (
    .Instruction(in_3), .ALUControl(controlunit_1_alucontrol));  // open: RegWrite, ALUSrc, Branch
  ALU alu_1 (.F(controlunit_1_alucontrol), .B(in_2), .A(in_1), .Y(out_4));  // open: ZERO
endmodule

module ALU (
  input  [2:0] F,
  input  [31:0] B,
  input  [31:0] A,
  output ZERO,
  output [31:0] Y
);

  wire [31:0] adder_1_out, and_1_out, bit_extender_1_out, multiplexer_1_out, not_1_out, or_1_out;

  Multiplexer #(.width(32)) multiplexer_1 (.in0(B), .in1(not_1_out), .out(multiplexer_1_out), .sel(F[0]));
  assign not_1_out = ~B;  // NOT_Gate not_1, 32 bits wide
  assign and_1_out = B & A;  // AND_Gate and_1, 32 bits wide
  assign or_1_out = B | A;  // OR_Gate or_1, 32 bits wide
  Adder #(.width(32)) adder_1 (.a(multiplexer_1_out), .b(A), .out(adder_1_out), .cin(F[0]));  // open: cout
  assign bit_extender_1_out = {{31{1'b0}}, adder_1_out[31]};  // Bit_Extender bit_extender_1
  Multiplexer #(.select(3), .width(32)) multiplexer_2 (
    .in0(adder_1_out), .in1(adder_1_out), .in2(and_1_out), .in3(or_1_out), .in7(bit_extender_1_out), .out(Y),
    .sel(F));  // open: in4, in5, in6
  Comparator #(.mode("unsigned"), .width(32)) comparator_1 (.a({32{1'b0}}), .b(Y), .eq(ZERO));  // open: gt, lt

  // Notes on the sheet:
  //   Choose function
  //   Choose pos/neg input
  //   Carry in for msb sign extend + enable
  //   Zero extend to 32 bit
  //   Choose output from mux
endmodule

module Datapath (
  output [7:0] out_1,
  output [7:0] out_2,
  output [7:0] out_3,
  output [7:0] out_4,
  output [7:0] out_5,
  output [2:0] A3_RD,
  output [2:0] A2_RS2,
  output [2:0] A1_RS1,
  output [31:0] out_9,
  output [31:0] out_10,
  output [31:0] t2,
  output [31:0] out_12
);

  wire adder_2_cout, alu_1_zero, and_1_out, clock_1_out, controlunit_1_alusrc, controlunit_1_branch,
       controlunit_1_regwrite, undriven;
  wire [2:0] controlunit_1_alucontrol;
  wire [7:0] adder_1_out;
  wire [31:0] alu_1_y, multiplexer_2_out, registerfile_1_rd1, registerfile_1_rd2;

  Register register_1 (.D(out_4), .en(1'b1), .clk(clock_1_out), .Q(out_1));  // open: clr
  Adder adder_1 (.a(8'h4), .b(out_1), .out(adder_1_out));  // open: cin, cout
  Adder adder_2 (.a({out_3[7:3], A3_RD}), .b(out_1), .out(out_2), .cin(undriven), .cout(adder_2_cout));
  Multiplexer #(.width(8)) multiplexer_1 (.in0(adder_1_out), .in1(out_2), .out(out_4), .sel(and_1_out));
  Shifter #(.shift("lr")) shifter_1 (.in(out_1), .\dist (3'b010), .out(out_5));
  ROM #(.dataWidth(32)) rom_1 (
    .addr(out_5),
    .data({out_9[31:29], out_3[7:4], out_9[24:23], A2_RS2, out_9[19:18], A1_RS1, out_9[14:11], out_3[3], A3_RD, out_9[6:0]}));
  Clock clock_1 (.out(clock_1_out));
  assign out_10 = {{20{out_9[31]}}, {out_9[31:29], out_3[7:4], out_9[24:23], A2_RS2}};  // Bit_Extender bit_extender_1
  ControlUnit controlunit_1 (
    .Instruction({out_9[31:29], out_3[7:4], out_9[24:23], A2_RS2, out_9[19:18], A1_RS1, out_9[14:11], out_3[3], A3_RD, out_9[6:0]}),
    .RegWrite(controlunit_1_regwrite), .ALUSrc(controlunit_1_alusrc), .ALUControl(controlunit_1_alucontrol),
    .Branch(controlunit_1_branch));
  RegisterFile registerfile_1 (
    .A3(A3_RD), .WE3(controlunit_1_regwrite), .WD3(alu_1_y), .CLK(clock_1_out), .A2(A2_RS2), .A1(A1_RS1),
    .RD1(registerfile_1_rd1), .RD2(registerfile_1_rd2), .T2(t2));
  Multiplexer #(.width(32)) multiplexer_2 (
    .in0(registerfile_1_rd2), .in1(out_10), .out(multiplexer_2_out), .sel(controlunit_1_alusrc));
  and and_1 (and_1_out, alu_1_zero, controlunit_1_branch);
  ALU alu_1 (
    .F(controlunit_1_alucontrol), .B(multiplexer_2_out), .A(registerfile_1_rd1), .Y(alu_1_y),
    .ZERO(alu_1_zero));

  assign out_3[2:0] = A3_RD;
  assign {out_9[28:25], out_9[22:20], out_9[17:15], out_9[10:7]} = {out_3[7:4], A2_RS2, A1_RS1, out_3[3], A3_RD};
  assign out_12 = {out_9[31:29], out_3[7:4], out_9[24:23], A2_RS2, out_9[19:18], A1_RS1, out_9[14:11], out_3[3], A3_RD, out_9[6:0]};

  // Notes on the sheet:
  //   contents of rom_1 (hex, n*v repeats v):
  //   300293 2028e63 500233 333 130313 530663 7203b3 fe000ae3 333 fff28293 28863 700233 3b3 fc000ee3
  //   4003b3 663 100393 263 63
endmodule

module RegisterFile (
  input  CLK,
  input  [2:0] A1,
  input  [31:0] WD3,
  input  [2:0] A2,
  input  WE3,
  input  [2:0] A3,
  output [31:0] RD1,
  output [31:0] RD2,
  output [31:0] T2
);

  wire and_1_out, and_2_out, and_3_out, and_4_out, and_5_out, and_6_out, and_7_out, and_8_out,
       decoder_1_out0, decoder_1_out1, decoder_1_out2, decoder_1_out3, decoder_1_out4, decoder_1_out5,
       decoder_1_out6, decoder_1_out7;
  wire [31:0] gp_q, ra_q, sp_q, t0_q, t1_q, tp_q, Zero_q;

  Decoder #(.select(3)) decoder_1 (
    .out0(decoder_1_out0), .out1(decoder_1_out1), .out2(decoder_1_out2), .out3(decoder_1_out3),
    .out4(decoder_1_out4), .out5(decoder_1_out5), .out6(decoder_1_out6), .out7(decoder_1_out7), .sel(A3));  // open: en
  and and_1 (and_1_out, WE3, decoder_1_out0);
  and and_2 (and_2_out, WE3, decoder_1_out1);
  and and_3 (and_3_out, WE3, decoder_1_out2);
  and and_4 (and_4_out, WE3, decoder_1_out3);
  and and_5 (and_5_out, WE3, decoder_1_out4);
  and and_6 (and_6_out, WE3, decoder_1_out5);
  and and_7 (and_7_out, WE3, decoder_1_out6);
  and and_8 (and_8_out, WE3, decoder_1_out7);
  Register #(.width(32)) Zero (.D({32{1'b0}}), .en(and_1_out), .clk(CLK), .Q(Zero_q));  // open: clr
  Register #(.width(32)) ra (.D(WD3), .en(and_2_out), .clk(CLK), .Q(ra_q));  // open: clr
  Register #(.width(32)) sp (.D(WD3), .en(and_3_out), .clk(CLK), .Q(sp_q));  // open: clr
  Register #(.width(32)) gp (.D(WD3), .en(and_4_out), .clk(CLK), .Q(gp_q));  // open: clr
  Register #(.width(32)) tp (.D(WD3), .en(and_5_out), .clk(CLK), .Q(tp_q));  // open: clr
  Register #(.width(32)) t0 (.D(WD3), .en(and_6_out), .clk(CLK), .Q(t0_q));  // open: clr
  Register #(.width(32)) t1 (.D(WD3), .en(and_7_out), .clk(CLK), .Q(t1_q));  // open: clr
  Register #(.width(32)) t22 (.D(WD3), .en(and_8_out), .clk(CLK), .Q(T2));  // open: clr
  Multiplexer #(.enable("true"), .select(3), .width(32)) multiplexer_1 (
    .in0(Zero_q), .in1(ra_q), .in2(sp_q), .in3(gp_q), .in4(tp_q), .in5(t0_q), .in6(t1_q), .in7(T2),
    .out(RD1), .sel(A1));  // open: en
  Multiplexer #(.enable("true"), .select(3), .width(32)) multiplexer_2 (
    .in0(Zero_q), .in1(ra_q), .in2(sp_q), .in3(gp_q), .in4(tp_q), .in5(t0_q), .in6(t1_q), .in7(T2),
    .out(RD2), .sel(A2));  // open: en

  // Notes on the sheet:
  //   Choose which register
  //   Instruction
  //   Enable write to register
  //   Register update at rising edge
  //   Choose register to read from for rd1 and rd2
  //   MUX for choosing register
  //   Instruction stored in register t2
  //   Outputs read from chosen register
endmodule

module ControlUnit (
  input  [31:0] Instruction,
  output RegWrite,
  output ALUSrc,
  output [2:0] ALUControl,
  output Branch
);

  wire comparator_3_eq;

  Comparator #(.mode("unsigned"), .width(7)) comparator_1 (
    .a(Instruction[6:0]), .b(7'b1100011), .eq(Branch));  // open: gt, lt
  Comparator #(.mode("unsigned"), .width(7)) comparator_2 (
    .a(Instruction[6:0]), .b(7'b0010011), .eq(ALUSrc));  // open: gt, lt
  Comparator #(.mode("unsigned"), .width(7)) comparator_3 (
    .a(Instruction[6:0]), .b(7'b0110011), .eq(comparator_3_eq));  // open: gt, lt
  or or_1 (RegWrite, ALUSrc, comparator_3_eq);
  assign ALUControl = {{2{1'b0}}, Branch};  // Bit_Extender bit_extender_1

  // Notes on the sheet:
  //   Op bits (0-6) are 0b1100011=0x63 for beq instruction
  //   Zero extend output 1 (equals) to 001 to choose subtraction in ALU
  //   0x33 = 0b001100 which is R-type instruction -> AluSrc = 0 RegWrite =1
  //   0x13 = 0b0010011 which is I-type instruction -> ALUSrc and RegWrite = 1
endmodule

module Tests (
  output [31:0] Y,
  output [3:0] out_2,
  output [7:0] out_3
);


  assign out_2 = 4'b0010;
  assign out_3 = 8'h22;
  assign Y = 32'hf4010207;

  // Notes on the sheet:
  //   binary values in Logisim. Convince yourself how the bits are displayed.
  //   Example 1: A simple example that illustrates how 32-bit values are displayed as 
  //   Example 2) An example of how to extra certain bits from a (in this case) 32-bit wire. Here we extract the bits 8..11 from the 32-bit wire.
  //   Example 3) Sometimes it is useful to extra bits from different position and the re-assemble them. In this case, we extract bits 8..11 and bits 15..18 and assemble them into an 8-bit wire.
endmodule
